// Logisim project alu.circ as structural Verilog: 1 circuit, main circuit alu
module alu (
  input  [31:0] A,
  input  [31:0] B,
  input  [3:0] ALUSel,
  output [31:0] Result
);

  wire comparator_2_eq, comparator_3_eq, comparator_4_eq, comparator_5_eq, comparator_6_gt, comparator_7_gt,
       comparator_8_eq, comparator_9_eq;
  wire [0:0] mySLT;
  wire [5:0] adder_2_out, bitadder_1_out, bitadder_2_out;
  wire [31:0] add, and_2_out, multiplexer_1_out, multiplexer_2_out, multiplier_2_out, multiplier_3_out,
       multiplier_4_cout, myAND, myCNTO, myDIVU, myMULH, myMULHU, myMULT, myOR, myREMU, mySLL, mySRA, mySRL,
       mySUB, myXOR, negator_1_out, negator_2_out, or_2_out, subtractor_2_out;

  BitAdder #(.width(32)) bitadder_1 (.in0(A), .out(bitadder_1_out));
  BitAdder #(.width(32)) bitadder_2 (.in0(B), .out(bitadder_2_out));
  Adder #(.width(32)) adder_1 (.a(A), .b(B), .out(add));  // open: cin, cout
  Shifter #(.width(32), .shift("lr")) shifter_1 (.in(A), .\dist (B[4:0]), .out(mySRL));
  assign myAND = A & B;  // AND_Gate and_1, 32 bits wide
  Shifter #(.width(32), .shift("ar")) shifter_2 (.in(A), .\dist (B[4:0]), .out(mySRA));
  assign myOR = A | B;  // OR_Gate or_1, 32 bits wide
  Shifter #(.width(32)) shifter_3 (.in(A), .\dist (B[4:0]), .out(mySLL));
  assign myXOR = A ^ B;  // XOR_Gate xor_1, 32 bits wide
  Comparator #(.width(32)) comparator_1 (.a(A), .b(B), .lt(mySLT[0]));  // open: gt, eq
  Divider #(.width(32)) divider_1 (.a(A), .b(B), .out(myDIVU), .rem(myREMU));  // open: upper
  Multiplier #(.width(32)) multiplier_1 (.a(A), .b(B), .cout(myMULHU));  // open: out, cin
  Subtractor #(.width(32)) subtractor_1 (.a(A), .b(B), .out(mySUB));  // open: bin, bout
  Adder #(.width(6)) adder_2 (.a(bitadder_1_out), .b(bitadder_2_out), .out(adder_2_out));  // open: cin, cout
  assign myCNTO = {{26{1'b0}}, adder_2_out};  // Bit_Extender bit_extender_1
  Negator #(.width(32)) negator_1 (.in(A), .out(negator_1_out));
  Comparator #(.width(1)) comparator_2 (.a(A[31]), .b(1'b0), .eq(comparator_2_eq));  // open: gt, lt
  Negator #(.width(32)) negator_2 (.in(B), .out(negator_2_out));
  Comparator #(.width(1)) comparator_3 (.a(B[31]), .b(1'b0), .eq(comparator_3_eq));  // open: gt, lt
  Multiplier #(.width(32)) multiplier_2 (.a(A), .b(B), .out(multiplier_2_out));  // open: cin, cout
  Multiplier #(.width(32)) multiplier_3 (.a(A), .b(B), .out(multiplier_3_out));  // open: cin, cout
  Multiplexer #(.width(32), .enable("false")) multiplexer_1 (
    .in0(negator_1_out), .in1(A), .out(multiplexer_1_out), .sel(comparator_2_eq));
  Multiplexer #(.width(32), .enable("false")) multiplexer_2 (
    .in0(negator_2_out), .in1(B), .out(multiplexer_2_out), .sel(comparator_3_eq));
  Multiplexer #(.select(4), .width(32), .enable("false")) multiplexer_3 (
    .in0(add), .in1(myAND), .in2(myOR), .in3(myXOR), .in4(mySRL), .in5(mySRA), .in6(mySLL),
    .in7({{31{1'b0}}, mySLT[0]}), .in8(myDIVU), .in9(myREMU), .in10(myMULT), .in11(myMULHU), .in12(mySUB),
    .in13(myCNTO), .in14(myMULH), .out(Result), .sel(ALUSel));  // open: in15
  assign and_2_out = 32'h7fffffff & multiplier_2_out;  // AND_Gate and_2, 32 bits wide
  assign or_2_out = 32'h80000000 | multiplier_3_out;  // OR_Gate or_2, 32 bits wide
  Multiplier #(.width(32)) multiplier_4 (
    .a(multiplexer_1_out), .b(multiplexer_2_out), .cout(multiplier_4_cout));  // open: out, cin
  Comparator #(.width(1)) comparator_4 (.a(A[31]), .b(1'b0), .eq(comparator_4_eq));  // open: gt, lt
  Comparator #(.width(1)) comparator_5 (.a(B[31]), .b(1'b0), .eq(comparator_5_eq));  // open: gt, lt
  Multiplexer #(.width(32), .enable("false")) multiplexer_4 (
    .in0(or_2_out), .in1(and_2_out), .out(myMULT), .sel(comparator_9_eq));
  Comparator #(.width(32)) comparator_6 (.a(A), .b({32{1'b0}}), .gt(comparator_6_gt));  // open: eq, lt
  Comparator #(.width(32)) comparator_7 (.a(B), .b({32{1'b0}}), .gt(comparator_7_gt));  // open: eq, lt
  Subtractor #(.width(32)) subtractor_2 (
    .a({32{1'b1}}), .b(multiplier_4_cout), .out(subtractor_2_out));  // open: bin, bout
  Comparator #(.width(1)) comparator_8 (
    .a(comparator_4_eq), .b(comparator_5_eq), .eq(comparator_8_eq));  // open: gt, lt
  Comparator #(.width(1)) comparator_9 (
    .a(comparator_6_gt), .b(comparator_7_gt), .eq(comparator_9_eq));  // open: gt, lt
  Multiplexer #(.width(32), .enable("false")) multiplexer_5 (
    .in0(subtractor_2_out), .in1(multiplier_4_cout), .out(myMULH), .sel(comparator_8_eq));

  // Notes on the sheet:
  //   INPUTS to your circuit
  //   DON'T CHANGE THE LOCATIONS OF THE INPUTS AND OUTPUTS!
  //   OUTPUT from your circuit
endmodule
