// Logisim project cpu.circ as structural Verilog: 4 circuits, main circuit main
module main (
  input  [31:0] INSTRUCTION,
  input  CLOCK,
  output [31:0] FETCH_ADDRESS,
  output [31:0] ra,
  output [31:0] sp,
  output [31:0] t0,
  output [31:0] t1,
  output [31:0] t2,
  output [31:0] s0,
  output [31:0] s1,
  output [31:0] a0
);

  wire ASel, branchcomp_1_breq, branchcomp_1_brlt, BrUn, BSel, ControlLogic_memrw, PCSel, RegWEn;
  wire [1:0] ControlLogic_wbsel;
  wire [2:0] mydecoder_1_funct3, mydecoder_1_optype;
  wire [3:0] ALUSel;
  wire [4:0] mydecoder_1_rd, mydecoder_1_rs1, mydecoder_1_rs2;
  wire [6:0] mydecoder_1_funct7, mydecoder_1_opcode;
  wire [31:0] Arithmetic_Logic_Unit_result, DMEM_read_data, imm, multiplexer_1_out, multiplexer_2_out,
       multiplexer_3_out, pc4, RegFile_read_data_1, RegFile_read_data_2, undriven, WriteBack;

  Multiplexer #(.width(32), .enable("false")) multiplexer_1 (
    .in0(undriven), .in1(pc4), .out(multiplexer_1_out), .sel(PCSel));
  Register #(.width(32)) PC (.D(multiplexer_1_out), .clk(CLOCK), .Q(FETCH_ADDRESS));  // open: en, clr
  Adder #(.width(32)) adder_1 (.a(32'h1), .b(FETCH_ADDRESS), .out(pc4));  // open: cin, cout
  myDecoder mydecoder_1 (
    .DecoderIn(INSTRUCTION), .opcode(mydecoder_1_opcode), .funct7(mydecoder_1_funct7), .rs1(mydecoder_1_rs1),
    .rs2(mydecoder_1_rs2), .rd(mydecoder_1_rd), .funct3(mydecoder_1_funct3), .imm(imm),
    .opType(mydecoder_1_optype));
  regfile_main RegFile (
    .Read_Register_1_rs1(mydecoder_1_rs1), .Read_Register_2_rs2(mydecoder_1_rs2),
    .Write_Register_rd(mydecoder_1_rd), .Write_Data(WriteBack), .Write_Enable(RegWEn), .Clock(CLOCK),
    .Read_Data_1(RegFile_read_data_1), .Read_Data_2(RegFile_read_data_2));  // open: ra, sp, t0, t1, t2, s0, s1, a0
  myController ControlLogic (
    .Inst32(INSTRUCTION), .opcode(mydecoder_1_opcode), .funct7(mydecoder_1_funct7),
    .funct3(mydecoder_1_funct3), .opType(mydecoder_1_optype), .BrEq(branchcomp_1_breq),
    .BrLT(branchcomp_1_brlt), .BSel(BSel), .PCSel(PCSel), .BrUn(BrUn), .ASel(ASel), .RegWEn(RegWEn),
    .MemRW(ControlLogic_memrw), .WBSel(ControlLogic_wbsel), .ALUSel(ALUSel));
  Multiplexer #(.width(32), .enable("false")) multiplexer_2 (
    .in0(RegFile_read_data_1), .in1(FETCH_ADDRESS), .out(multiplexer_2_out), .sel(ASel));
  BranchComp branchcomp_1 (
    .DataA(RegFile_read_data_1), .DataB(RegFile_read_data_2), .BrUn(BrUn), .BrEq(branchcomp_1_breq),
    .BrLT(branchcomp_1_brlt));
  Multiplexer #(.width(32), .enable("false")) multiplexer_3 (
    .in0(RegFile_read_data_2), .in1(imm), .out(multiplexer_3_out), .sel(BSel));
  Multiplexer #(.select(2), .width(32), .enable("false")) multiplexer_4 (
    .in0(Arithmetic_Logic_Unit_result), .in1(DMEM_read_data), .in2(pc4), .out(WriteBack),
    .sel(ControlLogic_wbsel));  // open: in3
  mem_main DMEM (
    .Address(Arithmetic_Logic_Unit_result), .Write_Data(RegFile_read_data_2), .Write_En(ControlLogic_memrw),
    .Read_Data(DMEM_read_data), .clk(CLOCK));
  alu Arithmetic_Logic_Unit (
    .A(multiplexer_2_out), .B(multiplexer_3_out), .ALUSel(ALUSel), .Result(Arithmetic_Logic_Unit_result));

  // Other names for the same wires on the sheet: clk = CLOCK; fetch_addr[31:0] = FETCH_ADDRESS;
  //   pc[31:0] = FETCH_ADDRESS

  // Notes on the sheet:
  //   Output
  //   Inputs/Outputs from run.circ. DO NOT MOVE THESE.
  //   Inputs
  //   Inputs/Outputs from run.circ. DO NOT MOVE THESE.
endmodule

module myDecoder (
  input  [31:0] DecoderIn,
  output [6:0] opcode,
  output [6:0] funct7,
  output [4:0] rs1,
  output [4:0] rs2,
  output [4:0] rd,
  output [2:0] funct3,
  output [31:0] imm,
  output [2:0] opType
);

  wire comparator_1_eq, comparator_2_eq, comparator_3_eq, comparator_4_eq, comparator_5_eq, comparator_6_eq,
       comparator_7_eq, comparator_8_eq;
  wire [31:0] I, S, SB, UJ;

  assign S = {{20{1'b0}}, {DecoderIn[31:25], DecoderIn[11:7]}};  // Bit_Extender bit_extender_1
  assign I = {{20{1'b0}}, DecoderIn[31:20]};  // Bit_Extender bit_extender_2
  assign SB = {{19{1'b0}}, {DecoderIn[31], DecoderIn[7], DecoderIn[30:25], DecoderIn[11:8], 1'b0}};  // Bit_Extender bit_extender_3
  Comparator #(.width(7), .mode("unsigned")) comparator_1 (
    .a(DecoderIn[6:0]), .b(7'b0000011), .eq(comparator_1_eq));  // open: gt, lt
  Comparator #(.width(7), .mode("unsigned")) comparator_2 (
    .a(DecoderIn[6:0]), .b(7'b0010011), .eq(comparator_2_eq));  // open: gt, lt
  Comparator #(.width(7), .mode("unsigned")) comparator_3 (
    .a(DecoderIn[6:0]), .b(7'b0100011), .eq(comparator_3_eq));  // open: gt, lt
  Comparator #(.width(7), .mode("unsigned")) comparator_4 (
    .a(DecoderIn[6:0]), .b(7'b0110011), .eq(comparator_4_eq));  // open: gt, lt
  assign UJ = {{11{1'b0}}, {DecoderIn[31], DecoderIn[19:12], DecoderIn[20], DecoderIn[30:21], 1'b0}};  // Bit_Extender bit_extender_4
  Comparator #(.width(7), .mode("unsigned")) comparator_5 (
    .a(DecoderIn[6:0]), .b(7'b1100011), .eq(comparator_5_eq));  // open: gt, lt
  Comparator #(.width(7), .mode("unsigned")) comparator_6 (
    .a(DecoderIn[6:0]), .b(7'b0110111), .eq(comparator_6_eq));  // open: gt, lt
  Comparator #(.width(7), .mode("unsigned")) comparator_7 (
    .a(DecoderIn[6:0]), .b(7'b1101111), .eq(comparator_7_eq));  // open: gt, lt
  Comparator #(.width(7), .mode("unsigned")) comparator_8 (
    .a(DecoderIn[6:0]), .b(7'b1100111), .eq(comparator_8_eq));  // open: gt, lt
  Multiplexer #(.select(3), .width(32), .enable("false")) multiplexer_1 (
    .in0(SB), .in1({DecoderIn[31:12], {12{1'b0}}}), .in2(UJ), .in3(I), .in4(I), .in5(I), .in6(S),
    .in7({32{1'b0}}), .out(imm), .sel(opType));
  Priority_Encoder priority_encoder_1 (
    .in0(comparator_5_eq), .in1(comparator_6_eq), .in2(comparator_7_eq), .in3(comparator_8_eq),
    .in4(comparator_1_eq), .in5(comparator_2_eq), .in6(comparator_3_eq), .in7(comparator_4_eq), .out(opType));  // open: en_in, gs, en_out

  assign funct3 = DecoderIn[14:12];
  assign funct7 = DecoderIn[31:25];
  assign opcode = DecoderIn[6:0];
  assign rd = DecoderIn[11:7];
  assign rs1 = DecoderIn[19:15];
  assign rs2 = DecoderIn[24:20];

  // Other names for the same wires on the sheet: DecoderInput[31:0] = DecoderIn; U[31:12] = DecoderIn[31:12]
endmodule

module myController (
  input  [31:0] Inst32,
  input  [6:0] opcode,
  input  [6:0] funct7,
  input  [2:0] funct3,
  input  [2:0] opType,
  input  BrEq,
  input  BrLT,
  output BSel,
  output PCSel,
  output BrUn,
  output ASel,
  output RegWEn,
  output MemRW,
  output [1:0] WBSel,
  output [3:0] ALUSel
);

  wire and_1_out, beq_out, blt_out, bltu_out, bne_out, comparator_3_eq, comparator_4_eq, comparator_5_eq,
       comparator_6_eq, comparator_7_eq, comparator_8_eq, comparator_9_eq, comparator_9_lt, comparator_11_eq,
       comparator_11_lt, comparator_13_eq, not_1_out, or_1_out;

  Comparator #(.width(3)) comparator_1 (.a(opType), .b(3'b100));  // open: gt, eq, lt
  Comparator #(.width(3)) comparator_2 (.a(opType), .b(3'b101));  // open: gt, eq, lt
  Comparator #(.width(3)) comparator_3 (.a(opType), .b(3'b110), .eq(comparator_3_eq));  // open: gt, lt
  Comparator #(.width(3)) comparator_4 (
    .a(opType), .b(3'b111), .eq(comparator_4_eq), .lt(comparator_4_eq));  // open: gt
  Comparator #(.width(3)) comparator_5 (.a(funct3), .b(3'b000), .eq(comparator_5_eq));  // open: gt, lt
  Comparator #(.width(3)) comparator_6 (.a(funct3), .b(3'b110), .eq(comparator_6_eq));  // open: gt, lt
  Comparator #(.width(3)) comparator_7 (.a(funct3), .b(3'b100), .eq(comparator_7_eq));  // open: gt, lt
  Comparator #(.width(3)) comparator_8 (.a(funct3), .b(3'b001), .eq(comparator_8_eq));  // open: gt, lt
  not not_1 (not_1_out, BrEq);
  and beq (beq_out, comparator_5_eq, BrEq);
  and bltu (bltu_out, comparator_6_eq, BrLT);
  and blt (blt_out, comparator_7_eq, BrLT);
  and bne (bne_out, comparator_8_eq, not_1_out);
  Comparator #(.width(3)) comparator_9 (
    .a(opType), .b(3'b000), .eq(comparator_9_eq), .lt(comparator_9_lt));  // open: gt
  Comparator #(.width(3)) comparator_10 (.a(opType), .b(3'b001));  // open: gt, eq, lt
  Comparator #(.width(3)) comparator_11 (
    .a(opType), .b(3'b010), .eq(comparator_11_eq), .lt(comparator_11_lt));  // open: gt
  Comparator #(.width(3)) comparator_12 (.a(opType), .b(3'b011));  // open: gt, eq, lt
  or or_1 (or_1_out, beq_out, bltu_out, blt_out, bne_out);
  Multiplexer #(.enable("false")) multiplexer_1 (.in0(1'b0), .in1(1'b1), .out(PCSel), .sel(and_1_out));
  and and_1 (and_1_out, comparator_9_eq, or_1_out);
  and and_2 (BrUn, comparator_9_eq, bltu_out);
  or or_2 (ASel, comparator_9_eq, comparator_11_eq);
  and and_3 (MemRW, comparator_3_eq, comparator_13_eq);
  Comparator #(.width(3)) comparator_13 (.a(funct3), .b(3'b010), .eq(comparator_13_eq));  // open: gt, lt
  not not_2 (BSel, comparator_4_eq);
  nor nor_1 (RegWEn, comparator_9_eq, MemRW);
endmodule

module BranchComp (
  input  [31:0] DataA,
  input  [31:0] DataB,
  input  BrUn,
  output BrEq,
  output BrLT
);

  wire comparator_1_eq, comparator_1_lt, comparator_2_eq, comparator_2_lt;

  Comparator #(.width(32), .mode("unsigned")) comparator_1 (
    .a(DataA), .b(DataB), .eq(comparator_1_eq), .lt(comparator_1_lt));  // open: gt
  Comparator #(.width(32)) comparator_2 (.a(DataA), .b(DataB), .eq(comparator_2_eq), .lt(comparator_2_lt));  // open: gt
  Multiplexer #(.enable("false")) multiplexer_1 (.in0(comparator_1_eq), .in1(comparator_2_eq), .out(BrEq), .sel(BrUn));
  Multiplexer #(.enable("false")) multiplexer_2 (.in0(comparator_1_lt), .in1(comparator_2_lt), .out(BrLT), .sel(BrUn));
endmodule
