// Logisim project regfile.circ as structural Verilog: 1 circuit, main circuit main
module main (
  input  [4:0] Read_Register_1_rs1,
  input  [4:0] Read_Register_2_rs2,
  input  [4:0] Write_Register_rd,
  input  [31:0] Write_Data,
  input  Write_Enable,
  input  Clock,
  output [31:0] ra,
  output [31:0] sp,
  output [31:0] t0,
  output [31:0] t1,
  output [31:0] t2,
  output [31:0] s0,
  output [31:0] s1,
  output [31:0] a0,
  output [31:0] Read_Data_1,
  output [31:0] Read_Data_2
);

  wire comparator_1_eq, comparator_2_eq, comparator_3_eq, comparator_4_eq, comparator_5_eq, comparator_6_eq,
       comparator_7_eq, comparator_8_eq;
  wire [31:0] demultiplexer_1_out1, demultiplexer_1_out2, demultiplexer_1_out5, demultiplexer_1_out6,
       demultiplexer_1_out7, demultiplexer_1_out8, demultiplexer_1_out9, demultiplexer_1_out10,
       multiplexer_1_out, multiplexer_2_out, multiplexer_3_out, multiplexer_4_out, multiplexer_5_out,
       multiplexer_6_out, multiplexer_7_out, multiplexer_8_out, register_5_q;

  // Probe on Write_Data
  Demultiplexer #(.select(4), .width(32), .enable("false")) demultiplexer_1 (
    .out1(demultiplexer_1_out1), .out2(demultiplexer_1_out2), .out5(demultiplexer_1_out5),
    .out6(demultiplexer_1_out6), .out7(demultiplexer_1_out7), .out8(demultiplexer_1_out8),
    .out9(demultiplexer_1_out9), .out10(demultiplexer_1_out10), .in(Write_Data), .sel(Write_Register_rd[3:0]));  // open: out0, out3, out4, out11, out12, out13, out14, out15
  // Probe on Write_Register_rd
  Multiplexer #(.width(32), .enable("false")) multiplexer_1 (
    .in0(demultiplexer_1_out1), .in1(ra), .out(multiplexer_1_out), .sel(comparator_1_eq));
  Comparator #(.width(32)) comparator_1 (
    .a(demultiplexer_1_out1), .b({32{1'b0}}), .eq(comparator_1_eq));  // open: gt, lt
  Multiplexer #(.width(32), .enable("false")) multiplexer_2 (
    .in0(demultiplexer_1_out2), .in1(sp), .out(multiplexer_2_out), .sel(comparator_2_eq));
  Comparator #(.width(32)) comparator_2 (
    .a(demultiplexer_1_out2), .b({32{1'b0}}), .eq(comparator_2_eq));  // open: gt, lt
  Multiplexer #(.width(32), .enable("false")) multiplexer_3 (
    .in0(demultiplexer_1_out5), .in1(t0), .out(multiplexer_3_out), .sel(comparator_3_eq));
  Comparator #(.width(32)) comparator_3 (
    .a(demultiplexer_1_out5), .b({32{1'b0}}), .eq(comparator_3_eq));  // open: gt, lt
  Multiplexer #(.width(32), .enable("false")) multiplexer_4 (
    .in0(demultiplexer_1_out6), .in1(t1), .out(multiplexer_4_out), .sel(comparator_4_eq));
  Comparator #(.width(32)) comparator_4 (
    .a(demultiplexer_1_out6), .b({32{1'b0}}), .eq(comparator_4_eq));  // open: gt, lt
  Register #(.width(32)) register_1 (.D(multiplexer_1_out), .en(Write_Enable), .clk(Clock), .Q(ra));  // open: clr
  Register #(.width(32)) register_2 (.D(multiplexer_2_out), .en(Write_Enable), .clk(Clock), .Q(sp));  // open: clr
  Register #(.width(32)) register_3 (.D(multiplexer_3_out), .en(Write_Enable), .clk(Clock), .Q(t0));  // open: clr
  Register #(.width(32)) register_4 (.D(multiplexer_4_out), .en(Write_Enable), .clk(Clock), .Q(t1));  // open: clr
  Register #(.width(32)) register_5 (.D({32{1'b0}}), .en(Write_Enable), .clk(Clock), .Q(register_5_q));  // open: clr
  Comparator #(.width(32)) comparator_5 (
    .a(demultiplexer_1_out7), .b({32{1'b0}}), .eq(comparator_5_eq));  // open: gt, lt
  Comparator #(.width(32)) comparator_6 (
    .a(demultiplexer_1_out8), .b({32{1'b0}}), .eq(comparator_6_eq));  // open: gt, lt
  Comparator #(.width(32)) comparator_7 (
    .a(demultiplexer_1_out9), .b({32{1'b0}}), .eq(comparator_7_eq));  // open: gt, lt
  Comparator #(.width(32)) comparator_8 (
    .a(demultiplexer_1_out10), .b({32{1'b0}}), .eq(comparator_8_eq));  // open: gt, lt
  Register #(.width(32)) register_6 (.D(multiplexer_5_out), .en(Write_Enable), .clk(Clock), .Q(t2));  // open: clr
  Multiplexer #(.width(32), .enable("false")) multiplexer_5 (
    .in0(demultiplexer_1_out7), .in1(t2), .out(multiplexer_5_out), .sel(comparator_5_eq));
  Register #(.width(32)) register_7 (.D(multiplexer_6_out), .en(Write_Enable), .clk(Clock), .Q(s0));  // open: clr
  Multiplexer #(.width(32), .enable("false")) multiplexer_6 (
    .in0(demultiplexer_1_out8), .in1(s0), .out(multiplexer_6_out), .sel(comparator_6_eq));
  Register #(.width(32)) register_8 (.D(multiplexer_7_out), .en(Write_Enable), .clk(Clock), .Q(s1));  // open: clr
  Multiplexer #(.width(32), .enable("false")) multiplexer_7 (
    .in0(demultiplexer_1_out9), .in1(s1), .out(multiplexer_7_out), .sel(comparator_7_eq));
  Register #(.width(32)) register_9 (.D(multiplexer_8_out), .en(Write_Enable), .clk(Clock), .Q(a0));  // open: clr
  Multiplexer #(.width(32), .enable("false")) multiplexer_8 (
    .in0(demultiplexer_1_out10), .in1(a0), .out(multiplexer_8_out), .sel(comparator_8_eq));
  Multiplexer #(.select(4), .width(32), .enable("false")) multiplexer_9 (
    .in0(register_5_q), .in1(ra), .in2(sp), .in5(t0), .in6(t1), .in7(t2), .in8(s0), .in9(s1), .in10(a0),
    .out(Read_Data_1), .sel(Read_Register_1_rs1[3:0]));  // open: in3, in4, in11, in12, in13, in14, in15
  Multiplexer #(.select(4), .width(32), .enable("false")) multiplexer_10 (
    .in0(register_5_q), .in1(ra), .in2(sp), .in5(t0), .in6(t1), .in7(t2), .in8(s0), .in9(s1), .in10(a0),
    .out(Read_Data_2), .sel(Read_Register_2_rs2[3:0]));  // open: in3, in4, in11, in12, in13, in14, in15

  // Other names for the same wires on the sheet: clk = Clock; read_data1[31:0] = Read_Data_1;
  //   read_data2[31:0] = Read_Data_2; read_reg1[4:0] = Read_Register_1_rs1; read_reg2[4:0] = Read_Register_2_rs2;
  //   write_en = Write_Enable; write_reg[4:0] = Write_Register_rd

  // Notes on the sheet:
  //   INPUTS to your circuit
  //   DON'T CHANGE THE LOCATIONS OF THE INPUTS AND OUTPUTS!
  //   These are DEBUG/TEST outputs from your circuit.
  //   OUTPUTS from your circuit
endmodule
